// Logisim project serial_adder.circ as structural Verilog: 1 circuit, main circuit main
module main (
  output A1,
  output A2,
  output A3,
  output A4,
  output B1,
  output B2,
  output B3,
  output B4
);

  wire n74283_1_p1, n74283_1_p2, n74283_1_p3, undriven, undriven_2;

  // _74283 74283_1: pin names not known; wires that end beside it: n74283_1_p1, n74283_1_p2, n74283_1_p3
  LED S1 (.in(undriven));
  LED S2 (.in(n74283_1_p3));
  LED S3 (.in(n74283_1_p1));
  LED S4 (.in(n74283_1_p2));
  LED Carry (.in(undriven_2));
endmodule
